# Fritzing sketch MPU6050 (saved by Fritzing 0.9.3b)

parts:
  GY1 = MPU-6050 Board GY-521 [form="♀ (female)" package=THT]
  Part1 = Arduino Nano (Rev3.0) (ICSP)

nets:
  N1: GY1.pin1, Part1.5V
  N2: GY1.pin2, Part1.GND
  N3: GY1.pin3, Part1.A4
  N4: GY1.pin4, Part1.A5

custom parts:
  MPU-6050 Board GY-521: Acelerometro y Giroscopio MPU-6050 Board GY-521
