# Fritzing sketch circuit_diagram (saved by Fritzing 0.9.3b)
breadboards: 1

parts:
  Part1 = Bluetooth HC-05 Macho
  Part3 = Jtron 1 Channel Optoisolated Relay Module [package=relay]
  Part2 = Arduino Uno (Rev3) - ICSP

nets:
  N1: Part1.TXD, Part2.D0/RX
  N2: Part1.RXD, Part2.D1/TX
  VCC: Part1.VCC, Part3.VCC, Part2.5V
  GND: Part1.GND, Part3.GND, Part2.GND
  N3: Part3.IN1, Part2.D7
